# Fritzing sketch Electronics_diagrams_Tag_Reader (saved by Fritzing 0.9.6b)

parts:
  Composant1 = Arduino Nano (Rev3.0)
  Composant3 = RFID USB Reader
  MCU1 = Raspberry Pi Zero
  LED1 = smd LED [color="Green (555nm)" package="1206 [SMD]"]
  LED2 = smd LED [color="Red (635nm)" package="1206 [SMD]"]
  Grove1 = Grove OLED 128x96
  R1 = Resistor [tolerance=±5% resistance=220 package="0402 [SMD]"]
  R2 = Resistor [tolerance=±5% resistance=220 package="0402 [SMD]"]
  Mod1 = Passive Buzzer

nets:
  N1: Composant1.D9, Composant3.GND
  N2: Composant1.D10, Composant3.GNDT
  N3: Composant1.D11/MOSI, Composant3.ANT2
  N4: Composant1.D12/MISO, Composant3.ANT1
  N5: Composant1.GND, Composant3.TX-O
  3V3: Composant1.AREF, Composant1.3V3, Composant3.VCC
  N6: Composant1.D13/SCK, Composant3.CP
  N7: MCU1.pin_1, Grove1.VCC
  N8: MCU1.pin_3, Grove1.SCL
  N9: MCU1.pin_5, Grove1.SDA
  N10: MCU1.pin_6, MCU1.pin_9, MCU1.pin_14, MCU1.pin_20, LED1.cathode, LED2.cathode, Grove1.GND, Mod1.-
  N11: MCU1.pin_11, R1.Pin_1
  N12: MCU1.pin_13, R2.Pin_1
  N13: MCU1.pin_15, Mod1.NC

notes:
  Arduino Nano V3.0 + RFID RC522
  Raspberry Pi Zero + OLED Screen + LEDs + Buzzer
